# Fritzing sketch ch07_led_switch_complete (saved by Fritzing 1.0.6)
circuit board: 8.46667cm x 5.64444cm
breadboards: 1

parts:
  S1 = Pushbutton [package=THT]
  LED1 = LED - 5mm [color="Red (633nm)" current=0.030A package="5 mm [THT]"]
  BAT1 = Battery Holders [package=lipo-1100mAh]
  R1 = Resistor [tolerance=±5% power=0.25W resistance=220 package=THT]

nets:
  N1: S1.leg0, R1.Pin_0
  N2: S1.leg1, BAT1.+
  N3: LED1.cathode, BAT1.-
  N4: LED1.anode, R1.Pin_1
